# Fritzing sketch dht22_5sensor (saved by Fritzing 0.9.3b)
breadboards: 1

parts:
  Componente1 = Arduino Uno (Rev3)
  DHT22_sensor_5 = Humidity and Temperature Sensor RHT03
  DHT22_sensor_4 = Humidity and Temperature Sensor RHT03
  DHT22_sensor_3 = Humidity and Temperature Sensor RHT03
  DHT22_sensor_2 = Humidity and Temperature Sensor RHT03
  DHT22_sensor_1 = Humidity and Temperature Sensor RHT03
  S1 = Pushbutton [package="[THT]"]
  R1 = Resistor [tolerance=±5% resistance=1k package=THT]
  R2 = Resistor [tolerance=±5% resistance=10k package=THT]
  R4 = Resistor [tolerance=±5% resistance=10k package=THT]
  R3 = Resistor [tolerance=±5% resistance=10k package=THT]
  R5 = Resistor [tolerance=±5% resistance=10k package=THT]
  R6 = Resistor [tolerance=±5% resistance=10k package=THT]

nets:
  N1: Componente1.D8, DHT22_sensor_4.Data-signal, R5.Pin_1
  N2: Componente1.D12/MISO, DHT22_sensor_5.Data-signal, R6.Pin_1
  N3: Componente1.D2, DHT22_sensor_1.Data-signal, R2.Pin_1
  N4: Componente1.D4, DHT22_sensor_2.Data-signal, R3.Pin_1
  N5: Componente1.D6_PWM, S1.Pin_1, S1.Pin_2, R1.Pin_0
  N6: Componente1.D7, DHT22_sensor_3.Data-signal, R4.Pin_1
  VCC: Componente1.5V, DHT22_sensor_5.Vcc, DHT22_sensor_4.Vcc, DHT22_sensor_3.Vcc, DHT22_sensor_2.Vcc, DHT22_sensor_1.Vcc, S1.Pin_3, S1.Pin_4, R2.Pin_0, R4.Pin_0, R3.Pin_0, R5.Pin_0, R6.Pin_0
  N7: Componente1.GND, DHT22_sensor_5.GND_2, DHT22_sensor_4.GND_2, DHT22_sensor_3.GND_2, DHT22_sensor_2.GND_2, DHT22_sensor_1.GND_2, R1.Pin_1
